# Fritzing sketch uklad (saved by Fritzing 0.9.0b)
breadboards: 1

parts:
  Part1 = Arduino Uno (Rev3)
  IC1 = IC, DIP package, 4 pins [chip_label=TR]
  R3 = Resistor [tolerance=±5% resistance=10k package=THT]
  R12 = Resistor [tolerance=±5% resistance=220 package=THT]
  LED1 = LED - 5mm [color="Red (633nm)" package="5 mm [THT]"]
  LED2 = LED - 5mm [color="Red (633nm)" package="5 mm [THT]"]
  LED3 = LED - 5mm [color="Green (555nm)" package="5 mm [THT]"]
  R13 = Resistor [tolerance=±5% resistance=220 package=THT]
  R14 = Resistor [tolerance=±5% resistance=220 package=THT]
  R15 = Resistor [tolerance=±5% resistance=220 package=THT]
  J1 = Basic Servo

nets:
  N1: Part1.A0, IC1.pin3, R3.Pin_0
  N2: Part1.D8, J1.pulse
  N3: Part1.D10_PWM/SS, LED2.anode
  N4: Part1.D11_PWM/MOSI, LED1.anode
  N5: Part1.D12/MISO, LED3.anode
  5V: Part1.5V, IC1.pin2, R12.Pin_1, J1.vcc
  GND: Part1.GND, IC1.pin1, R3.Pin_1, R13.Pin_0, R14.Pin_0, R15.Pin_0, J1.gnd
  N6: IC1.pin4, R12.Pin_0
  N7: LED1.cathode, R14.Pin_1
  N8: LED2.cathode, R13.Pin_1
  N9: LED3.cathode, R15.Pin_1
