# Fritzing sketch 01_led (saved by Fritzing 0.9.0b)
breadboards: 1

parts:
  Part1 = Arduino Uno (Rev3)
  LED1 = LED - 5mm [color="Orange (605nm)" package="5 mm [THT]"]
  LED2 = LED - 5mm [color="Green (570nm)" package="5 mm [THT]"]
  R1 = Resistor [tolerance=±5% resistance=220 package=THT]
  R4 = Resistor [tolerance=±5% resistance=220 package=THT]

nets:
  N1: Part1.D4, LED2.anode
  N2: Part1.D7, LED1.anode
  N3: Part1.GND, R1.Pin_0, R4.Pin_0
  N4: LED1.cathode, R4.Pin_1
  N5: LED2.cathode, R1.Pin_1
