# Fritzing sketch 01_solar_full_auto (saved by Fritzing 0.9.0b)
breadboards: 1
perfboards: 1

parts:
  Part1 = Arduino Uno (Rev3)
  U1 = Battery Holders [package=battery-aa-panel]
  J1 = Basic Servo
  J2 = Basic Servo
  R7 = Photocell (LDR) [package=THT]
  R8 = Photocell (LDR) [package=THT]
  R9 = Photocell (LDR) [package=THT]
  R10 = Photocell (LDR) [package=THT]

nets:
  N1: Part1.A4/SDA, R7.pin_1, R8.pin_1
  N2: Part1.A5/SCL, R9.pin_0, R10.pin_0
  N3: Part1.D9_PWM, J1.pulse
  N4: Part1.D10_PWM/SS, J2.pulse
  GND: Part1.GND, U1.-, J1.gnd, J2.gnd, R7.pin_0, R10.pin_1
  VCC: U1.+, J1.vcc, J2.vcc
  N5: R8.pin_0, R9.pin_1
