# Fritzing sketch 02_led_button (saved by Fritzing 0.9.0b)
breadboards: 1

parts:
  Part1 = Arduino Uno (Rev3)
  LED1 = LED - 5mm [color="Orange (605nm)" package="5 mm [THT]"]
  LED2 = LED - 5mm [color="Green (570nm)" package="5 mm [THT]"]
  R1 = Resistor [tolerance=±5% resistance=220 package=THT]
  R4 = Resistor [tolerance=±5% resistance=220 package=THT]
  R5 = Resistor [tolerance=±5% resistance=2.2k package=THT]
  S1 = Pushbutton [package="[THT]"]

nets:
  N1: Part1.D2, R5.Pin_1, S1.Pin_3, S1.Pin_4
  N2: Part1.D4, LED2.anode
  N3: Part1.D7, LED1.anode
  N4: Part1.5V, S1.Pin_1, S1.Pin_2
  N5: Part1.GND, R1.Pin_0, R4.Pin_0, R5.Pin_0
  N6: LED1.cathode, R4.Pin_1
  N7: LED2.cathode, R1.Pin_1
