# Fritzing sketch 04_solar_manual (saved by Fritzing 0.9.0b)
breadboards: 1

parts:
  Part1 = Arduino Uno (Rev3)
  LED1 = LED - 5mm [color="Orange (605nm)" package="5 mm [THT]"]
  LED2 = LED - 5mm [color="Green (570nm)" package="5 mm [THT]"]
  R1 = Resistor [tolerance=±5% resistance=220 package=THT]
  R4 = Resistor [tolerance=±5% resistance=220 package=THT]
  R5 = Resistor [tolerance=±5% resistance=2.2k package=THT]
  S1 = Pushbutton [package="[THT]"]
  R6 = Rotary Potentiometer (Small) [maximum_resistance=100kΩ package=THT]
  U1 = Battery Holders [package=battery-aa-panel]
  J1 = Basic Servo
  J2 = Basic Servo

nets:
  N1: Part1.A0, R6.wiper
  N2: Part1.D9_PWM, J1.pulse
  N3: Part1.D10_PWM/SS, J2.pulse
  N4: Part1.D2, R5.Pin_1, S1.Pin_3, S1.Pin_4
  N5: Part1.D4, LED2.anode
  N6: Part1.D7, LED1.anode
  N7: Part1.5V, S1.Pin_1, S1.Pin_2, R6.leg2
  GND: Part1.GND, R1.Pin_0, R4.Pin_0, R5.Pin_0, R6.leg1, U1.-, J1.gnd, J2.gnd
  N8: LED1.cathode, R4.Pin_1
  N9: LED2.cathode, R1.Pin_1
  VCC: U1.+, J1.vcc, J2.vcc
