# Fritzing sketch analog_input_pwm (saved by Fritzing 0.9.0b)
breadboards: 1

parts:
  Part1 = Arduino Nano (Rev3.0)
  R1 = Resistor [tolerance=±5% resistance=220 package=THT]
  LED1 = LED - 5mm [color="Red (633nm)" package="5 mm [THT]"]
  R3 = Rotary Potentiometer (Small) [maximum_resistance=10kΩ package=THT]

nets:
  N1: Part1.D11/MOSI, R1.Pin_1
  N2: Part1.GND, LED1.cathode, R3.leg2
  N3: Part1.5V, R3.leg1
  N4: Part1.A0, R3.wiper
  N5: R1.Pin_0, LED1.anode
