# Fritzing sketch A_09_czujnik_lini (saved by Fritzing 0.9.2b)
breadboards: 1

parts:
  LED1 = LED - 5mm [color="Red (633nm)" package="5 mm [THT]"]
  R1 = Resistor [tolerance=±5% resistance=220 package=THT]
  R3 = Rotary Potentiometer (Small) [maximum_resistance=100kΩ package=THT]
  IC3 = IC, DIP package, 14 pins [chip_label=TLC274CN]
  IC2 = IC, DIP package, 4 pins [chip_label=CNY70]
  R3_2 = Resistor [tolerance=±5% resistance=220 package=THT]
  R4 = Resistor [tolerance=±5% resistance=20k package=THT]

nets:
  N1: LED1.cathode, R1.Pin_1
  N2: LED1.anode, R3.leg1, IC3.pin11, IC2.pin1, IC2.pin3
  N3: R1.Pin_0, IC3.pin1
  N4: R3.wiper, IC3.pin3
  N5: R3.leg2, IC3.pin4, R3_2.Pin_0, R4.Pin_1
  N6: IC3.pin2, IC2.pin2, R4.Pin_0
  N7: IC2.pin4, R3_2.Pin_1

notes:
  5V
  GND
  napisy
