# Fritzing sketch ukladFritzing (saved by Fritzing 0.9.1b)
breadboards: 1

parts:
  R1 = Resistor [tolerance=±5% resistance=220 package=THT]
  R6 = Rotary Potentiometer (Small) [maximum_resistance=100kΩ package=THT]
  LED2 = LED - 5mm [color="Red (633nm)" package="5 mm [THT]"]
  IC4 = PICAXE-14M [package=THT]
  IC5 = IC, DIP package, 4 pins [chip_label=TR]
  R13 = Resistor [tolerance=±5% resistance=10k package=THT]
  R14 = Resistor [tolerance=±5% resistance=220 package=THT]

nets:
  N1: R1.Pin_0, R6.leg1, IC5.pin1
  N2: R1.Pin_1, LED2.cathode
  N3: R6.wiper, IC4.Serial_In
  N4: R6.leg2, IC4.In_3_/_Infrain, IC5.pin2
  N5: LED2.anode, IC4.+V
  N6: IC4.In_4_/_ADC_4, IC5.pin3, R13.Pin_0
  N7: IC4.Out_2, R13.Pin_1
  N8: IC5.pin4, R14.Pin_0
