# Fritzing sketch shift_register_7_led (saved by Fritzing 0.9.0b)
breadboards: 1

parts:
  Part2 = Arduino Nano (Rev3.0)
  R2 = Resistor [tolerance=±5% resistance=220 package=THT]
  U1 = 74HC595 [package="DIP16 [THT]"]
  7_Segment1 = 7 Segment Display
  R3 = Resistor [tolerance=±5% resistance=220 package=THT]
  R4 = Resistor [tolerance=±5% resistance=220 package=THT]
  R5 = Resistor [tolerance=±5% resistance=220 package=THT]
  R6 = Resistor [tolerance=±5% resistance=220 package=THT]
  R7 = Resistor [tolerance=±5% resistance=220 package=THT]
  R8 = Resistor [tolerance=±5% resistance=220 package=THT]

nets:
  GND: Part2.GND, U1.GND, U1.OE
  N1: Part2.D10, U1.DS
  N2: Part2.D11/MOSI, U1.ST_CP
  N3: Part2.D12/MISO, U1.SH_CP
  5V: Part2.5V, U1.MR, U1.VCC, 7_Segment1.common_anode
  N4: R2.Pin_0, 7_Segment1.Segment_B
  N5: R2.Pin_1, U1.Q1
  N6: U1.Q2, R3.Pin_1
  N7: U1.Q3, R4.Pin_1
  N8: U1.Q4, R5.Pin_1
  N9: U1.Q5, R6.Pin_1
  N10: U1.Q6, R7.Pin_1
  N11: U1.Q7, R8.Pin_1
  N12: 7_Segment1.Segment_E, R6.Pin_0
  N13: 7_Segment1.Segment_D, R7.Pin_0
  N14: 7_Segment1.Segment_C, R8.Pin_0
  N15: 7_Segment1.Segment_A, R3.Pin_0
  N16: 7_Segment1.Segment_F, R4.Pin_0
  N17: 7_Segment1.Segment_G, R5.Pin_0
